# Fritzing sketch lw_arduino (saved by Fritzing 0.8.5b)
breadboards: 1

parts:
  Part1 = Arduino Uno (Rev3)
  R1 = Resistor [tolerance=±5% resistance=220 package=THT]
  R2 = Resistor [tolerance=±5% resistance=220 package=THT]
  R3 = Resistor [tolerance=±5% resistance=220 package=THT]
  LED1 = RGB LED (6 legs) [package="5 mm [THT]"]

nets:
  N1: Part1.D10_PWM/SS, R2.Pin_1
  N2: Part1.D11_PWM/MOSI, R1.Pin_1
  GND: Part1.GND, LED1.GND
  N3: R1.Pin_0, LED1.Blue1
  N4: R2.Pin_0, LED1.Green
  N5: R3.Pin_0, LED1.Red
