# Fritzing sketch lw_arduino_4pin_common_anode (saved by Fritzing 0.9.2b)
breadboards: 1

parts:
  Part1 = Arduino Uno (Rev3)
  R1 = Resistor [tolerance=±5% resistance=68 package=THT]
  R2 = Resistor [tolerance=±5% resistance=68 package=THT]
  R3 = Resistor [tolerance=±5% resistance=100 package=THT]
  LED2 = RGB LED - (4 legs) [package="5 mm [THT]"]

nets:
  N1: Part1.D9_PWM, R3.Pin_1
  N2: Part1.D10_PWM/SS, R2.Pin_1, LED2.green_cathode
  N3: Part1.D11_PWM/MOSI, R1.Pin_1
  N4: Part1.5V, LED2.common_anode
  N5: R1.Pin_0, LED2.blue_cathode
  N6: R3.Pin_0, LED2.red_cathode
